// Digital circuit ALU.dig as structural Verilog
module ALU (
);

  wire comparator_1_eq, comparator_2_eq, comparator_3_eq, comparator_4_eq, comparator_5_eq, comparator_6_eq,
       comparator_7_eq, comparator_8_eq, comparator_9_eq, comparator_10_eq, comparator_11_eq,
       comparator_12_eq, comparator_13_eq, comparator_14_eq, comparator_15_eq, comparator_16_eq,
       comparator_17_eq, comparator_19_eq, comparator_20_eq, comparator_21_eq, comparator_22_eq,
       comparator_23_eq, comparator_24_eq, comparator_25_eq, comparator_26_eq, flag_register_1_p2,
       flag_register_1_p3, flag_register_1_p4, flag_register_1_p5, flag_register_1_p11, flag_register_1_p12,
       register_1_p1, register_1_p3, register_1_p4, register_2_p4;
  wire [7:0] undriven_26;
  wire [7:1] undriven, undriven_2, undriven_3, undriven_4, undriven_5, undriven_6, undriven_7, undriven_8,
       undriven_9, undriven_10, undriven_11, undriven_12, undriven_13, undriven_14, undriven_15, undriven_16,
       undriven_17, undriven_18, undriven_19, undriven_20, undriven_21, undriven_22, undriven_23,
       undriven_24, undriven_25;

  Comparator #(.Bits(8)) comparator_1 (.a(undriven_26), .b({undriven_23, 1'b1}), .eq(comparator_1_eq));  // open: gt, lt
  Comparator #(.Bits(8)) comparator_2 (.a(undriven_26), .b({undriven_24, 1'b1}), .eq(comparator_2_eq));  // open: gt, lt
  Comparator #(.Bits(8)) comparator_3 (.a(undriven_26), .b({undriven_25, 1'b1}), .eq(comparator_3_eq));  // open: gt, lt
  // Register register_1: pin names not known; wires that end beside it: register_1_p1, comparator_1_eq, register_1_p3, register_1_p4
  // Register register_2: pin names not known; wires that end beside it: register_1_p1, comparator_2_eq, register_1_p3, register_2_p4
  // Register register_3: pin names not known; wires that end beside it: register_1_p1, comparator_3_eq, register_1_p3, register_2_p4
  Comparator #(.Bits(8)) comparator_4 (.a(undriven_26), .b({undriven, 1'b1}), .eq(comparator_4_eq));  // open: gt, lt
  Comparator #(.Bits(8)) comparator_5 (.a(undriven_26), .b({undriven_2, 1'b1}), .eq(comparator_5_eq));  // open: gt, lt
  Comparator #(.Bits(8)) comparator_6 (.a(undriven_26), .b({undriven_3, 1'b1}), .eq(comparator_6_eq));  // open: gt, lt
  Comparator #(.Bits(8)) comparator_7 (.a(undriven_26), .b({undriven_4, 1'b1}), .eq(comparator_7_eq));  // open: gt, lt
  Comparator #(.Bits(8)) comparator_8 (.a(undriven_26), .b({undriven_5, 1'b1}), .eq(comparator_8_eq));  // open: gt, lt
  Comparator #(.Bits(8)) comparator_9 (.a(undriven_26), .b({undriven_6, 1'b1}), .eq(comparator_9_eq));  // open: gt, lt
  Comparator #(.Bits(8)) comparator_10 (
    .a(undriven_26), .b({undriven_7, 1'b1}), .eq(comparator_10_eq));  // open: gt, lt
  Comparator #(.Bits(8)) comparator_11 (
    .a(undriven_26), .b({undriven_8, 1'b1}), .eq(comparator_11_eq));  // open: gt, lt
  Comparator #(.Bits(8)) comparator_12 (
    .a(undriven_26), .b({undriven_9, 1'b1}), .eq(comparator_12_eq));  // open: gt, lt
  Comparator #(.Bits(8)) comparator_13 (
    .a(undriven_26), .b({undriven_10, 1'b1}), .eq(comparator_13_eq));  // open: gt, lt
  Comparator #(.Bits(8)) comparator_14 (
    .a(undriven_26), .b({undriven_11, 1'b1}), .eq(comparator_14_eq));  // open: gt, lt
  Comparator #(.Bits(8)) comparator_15 (
    .a(undriven_26), .b({undriven_12, 1'b1}), .eq(comparator_15_eq));  // open: gt, lt
  Comparator #(.Bits(8)) comparator_16 (
    .a(undriven_26), .b({undriven_13, 1'b1}), .eq(comparator_16_eq));  // open: gt, lt
  Comparator #(.Bits(8)) comparator_17 (
    .a(undriven_26), .b({undriven_14, 1'b1}), .eq(comparator_17_eq));  // open: gt, lt
  // Flag_Register flag_register_1: pin names not known; wires that end beside it: register_1_p1, flag_register_1_p2, flag_register_1_p3, flag_register_1_p4, flag_register_1_p5, comparator_4_eq, comparator_5_eq, comparator_6_eq, comparator_7_eq, register_1_p3, flag_register_1_p11, flag_register_1_p12
  // Adder_Subtractor adder_subtractor_1: pin names not known; wires that end beside it: flag_register_1_p12, register_1_p4, register_2_p4, comparator_8_eq, comparator_9_eq, comparator_10_eq, register_1_p3, flag_register_1_p11, flag_register_1_p2, flag_register_1_p3, flag_register_1_p4, flag_register_1_p5
  // Incrementor incrementor_1: pin names not known; wires that end beside it: register_2_p4, comparator_11_eq, comparator_12_eq, register_1_p3, flag_register_1_p11, flag_register_1_p2, flag_register_1_p3, flag_register_1_p4, flag_register_1_p5
  // Comparator comparator_18: pin names not known; wires that end beside it: register_1_p4, register_2_p4, comparator_13_eq, comparator_14_eq, comparator_15_eq, register_1_p3, flag_register_1_p11
  // Shift_Register shift_register_1: pin names not known; wires that end beside it: register_1_p1, register_1_p3, register_1_p4, register_1_p1, comparator_16_eq, comparator_17_eq, register_1_p3, flag_register_1_p11, flag_register_1_p11
  Comparator #(.Bits(8)) comparator_19 (
    .a(undriven_26), .b({undriven_15, 1'b1}), .eq(comparator_19_eq));  // open: gt, lt
  Comparator #(.Bits(8)) comparator_20 (
    .a(undriven_26), .b({undriven_16, 1'b1}), .eq(comparator_20_eq));  // open: gt, lt
  Comparator #(.Bits(8)) comparator_21 (
    .a(undriven_26), .b({undriven_17, 1'b1}), .eq(comparator_21_eq));  // open: gt, lt
  Comparator #(.Bits(8)) comparator_22 (
    .a(undriven_26), .b({undriven_18, 1'b1}), .eq(comparator_22_eq));  // open: gt, lt
  Comparator #(.Bits(8)) comparator_23 (
    .a(undriven_26), .b({undriven_19, 1'b1}), .eq(comparator_23_eq));  // open: gt, lt
  Comparator #(.Bits(8)) comparator_24 (
    .a(undriven_26), .b({undriven_20, 1'b1}), .eq(comparator_24_eq));  // open: gt, lt
  Comparator #(.Bits(8)) comparator_25 (
    .a(undriven_26), .b({undriven_21, 1'b1}), .eq(comparator_25_eq));  // open: gt, lt
  Comparator #(.Bits(8)) comparator_26 (
    .a(undriven_26), .b({undriven_22, 1'b1}), .eq(comparator_26_eq));  // open: gt, lt
  // Bitwise_NOT bitwise_not_1: pin names not known; wires that end beside it: register_1_p4, comparator_19_eq, register_1_p3, flag_register_1_p11
  // Bitwise_OR bitwise_or_1: pin names not known; wires that end beside it: register_1_p4, register_2_p4, comparator_20_eq, register_1_p3, flag_register_1_p11
  // Bitwise_AND bitwise_and_1: pin names not known; wires that end beside it: register_1_p4, register_2_p4, comparator_21_eq, register_1_p3, flag_register_1_p11
  // Bitwise_XOR bitwise_xor_1: pin names not known; wires that end beside it: register_1_p4, register_2_p4, comparator_22_eq, register_1_p3, flag_register_1_p11
  // Binary_NOT binary_not_1: pin names not known; wires that end beside it: register_1_p4, comparator_23_eq, register_1_p3, flag_register_1_p11
  // Binary_OR binary_or_1: pin names not known; wires that end beside it: register_1_p4, register_2_p4, comparator_24_eq, register_1_p3, flag_register_1_p11
  // Binary_AND binary_and_1: pin names not known; wires that end beside it: register_1_p4, register_2_p4, comparator_25_eq, register_1_p3, flag_register_1_p11
  // Binary_XOR binary_xor_1: pin names not known; wires that end beside it: register_2_p4, register_1_p1, register_1_p3, register_1_p4, register_2_p4, comparator_26_eq, register_1_p3, flag_register_1_p11, flag_register_1_p11
  // Pins of 1 and 8 bits meet at {undriven_5, 1'b1}
  // Pins of 1 and 8 bits meet at {undriven_6, 1'b1}
  // Pins of 1 and 8 bits meet at {undriven_7, 1'b1}
  // Pins of 1 and 8 bits meet at {undriven_10, 1'b1}
  // Pins of 1 and 8 bits meet at {undriven_11, 1'b1}
  // Pins of 1 and 8 bits meet at {undriven_12, 1'b1}
  // Pins of 1 and 8 bits meet at {undriven_15, 1'b1}
  // Pins of 1 and 8 bits meet at {undriven_16, 1'b1}
  // Pins of 1 and 8 bits meet at {undriven_17, 1'b1}
  // Pins of 1 and 8 bits meet at {undriven_18, 1'b1}
  // Pins of 1 and 8 bits meet at {undriven_21, 1'b1}
  // Pins of 1 and 8 bits meet at {undriven_19, 1'b1}

  // Notes on the sheet:
  //   CMD
  //   A
  //   B
  //   C
  //   DAT
  //   CLK
  //   Q
endmodule
