// Digital circuit Flash Memory.dig as structural Verilog
module Flash_Memory (
  input  [15:0] LN,
  output [7:0] CMD,
  output DAT,
  output ADR
);

  ROM #(.AddrBits(16), .Bits(8)) rom_1 (.A(LN), .sel(1'b1), .D(CMD));
  ROM #(.AddrBits(16), .Bits(8)) rom_2 (.A(LN), .sel(1'b1));  // open: D
  ROM #(.AddrBits(16), .Bits(16)) rom_3 (.A(LN), .sel(1'b1));  // open: D
  Comparator #(.Bits(8)) comparator_1 (.b(8'h11));  // open: a, gt, eq, lt
  Comparator #(.Bits(8)) comparator_2 (.b(8'h1e));  // open: a, gt, eq, lt
  Comparator #(.Bits(8)) comparator_3 (.b(8'h20));  // open: a, gt, eq, lt
  Comparator #(.Bits(8)) comparator_4 (.b(8'h22));  // open: a, gt, eq, lt
  Comparator #(.Bits(8)) comparator_5 (.b(8'h26));  // open: a, gt, eq, lt
  Comparator #(.Bits(8)) comparator_6 (.b(8'h27));  // open: a, gt, eq, lt
  Driver #(.Bits(8)) driver_1 ();  // open: in, en, out
  Driver #(.Bits(16)) driver_2 ();  // open: in, en, out
  // Or or_1 is placed but not wired
  // Pins of 1 and 16 bits meet at LN
  // Pins of 1 and 8 bits meet at CMD

  // Notes on the sheet:
  //   - Flash memory
endmodule
